# Fritzing sketch sensor (saved by Fritzing 0.9.2b)
perfboards: 1

parts:
  Teensy2 = Teensy 3.6 (Basic)
  JP2 = Header 2 [package=jst-2-smd]
  JP4 = Header 8 [package=1x08_smd_alt]
  JP6 = Header 8 [package=1x08_smd_alt]
  Part1 = Adafruit Ultimate GPS v3 [part_number="Adafruit #746"]
  JP7 = Header 6 [package=1x06_smd_straight_alt]
  JP8 = Header 6 [package=1x06_smd_straight_alt]  # not connected
  JP11 = Header 8 [package=1x08_smd_alt]
  JP12 = Header 6 [package=1x06_smd_straight_alt]  # not connected
  JP13 = Header 8 [package=1x08_smd_alt]
  R2 = Resistor [tolerance=±5% resistance=22k package="1206 [SMD]"]
  LED1 = smd LED [color="Red (633nm)" package="0603 [SMD]"]
  R1 = Resistor [tolerance=±5% resistance=220k package="1206 [SMD]"]
  R3 = Resistor [tolerance=±5% resistance=100 package="1206 [SMD]"]

nets:
  GND: Teensy2.GND, Teensy2.GND1, Part1.GND, JP7.2, JP11.6, JP13.6, R2.Pin_0, R3.Pin_1
  N1: Teensy2.D0, Part1.TX, JP7.4, JP13.5
  N2: Teensy2.D1, Part1.RX, JP7.3, JP13.4
  N3: Teensy2.A9/D23, JP4.3, LED1.anode
  3V3: Teensy2.3V3, Teensy2.3V3_1, JP2.1, JP6.6, Part1.VIN, JP7.1
  N4: Teensy2.D37, JP11.1
  N5: JP2.2, R1.Pin_1
  N6: R2.Pin_1, R1.Pin_0
  N7: LED1.cathode, R3.Pin_0

custom parts:
  Teensy 3.6 (Basic): The Teensy is a complete USB-based microcontoller development system, in a very small footprint, capable of implementing many types of projects. All programming is done via the USB port. No special programmer is needed, only a standard micro-USB cable and a PC or Macintosh with a USB port.
  Adafruit Ultimate GPS v3: We carry a few different GPS modules here in the Adafruit shop, but none that satisfied our every desire - that's why we designed this little GPS breakout board. We believe this is the Ultimate GPS module, so we named it that. It's got everything you want and more: -165 dBm sensitivity, 10 Hz updates, 66 channels 5V friendly design and only 20mA current draw Breadboard friendly + two mounting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
